# Fritzing sketch Anaire Prototipo MH-Z14a (saved by Fritzing 0.9.4)
breadboards: 1

parts:
  U1 = NodeMCU V1.0
  Mod1 = KY-015 Temperature & Humidity Sensor Module [package="Breakout board"]
  Mod2 = KY-016 RGB Full Color LED Module [package="Breakout board"]
  YwRobot_Power_Supply1 = YwRobot Breadboard Power Supply [part_number=545043]
  Mod3 = KY-012 Active Buzzer Module [package="Breakout board"]
  Mod4 = KY-004 Key Switch Module [package="Breakout board"]
  MH-Z1 = MH-Z14 [part_number=MH-Z14]

nets:
  N1: U1.D1, Mod1.S
  N2: U1.D2, Mod2.R
  N3: U1.D3, Mod2.G
  N4: U1.D4, Mod2.B
  N5: U1.GND, Mod1.-, YwRobot_Power_Supply1.GND#11, YwRobot_Power_Supply1.GND#12, Mod3.-
  N6: U1.D5, Mod4.S
  N7: U1.D6, Mod3.S
  N8: U1.D7, MH-Z1.10, MH-Z1.13
  N9: U1.D8, MH-Z1.14
  VIN: U1.Vin, Mod1.Vin, YwRobot_Power_Supply1.VCC#5, YwRobot_Power_Supply1.VCC#6, Mod3.NC
  N10: Mod2.-, YwRobot_Power_Supply1.GND#13, YwRobot_Power_Supply1.GND#14, Mod4.-, MH-Z1.2, MH-Z1.3
  N11: YwRobot_Power_Supply1.VCC#9, YwRobot_Power_Supply1.VCC#10, Mod4.Vin, MH-Z1.1, MH-Z1.15

custom parts:
  NodeMCU V1.0: ESP8266 based NodeMCU
  KY-015 Temperature & Humidity Sensor Module: KY-015 temperature and humidity sensor module, provides a low-latency serial interface to measure humidity and temperature.
  KY-016 RGB Full Color LED Module: KY-016 Arduino full color 5mm RGB LED, different colors can be obtained by mixing the three primary colors.
  YwRobot Breadboard Power Supply: The YwRobot Breadboard Power Supply (MB-V2) has two power rails; they can be 5V or 3V3. Power to the module can be provided through the female USB socket or through the A10 (female) 2.1mm power jack.
  KY-012 Active Buzzer Module: Active Piezoelectric Buzzer Module KY-012, it produces single-tone sound when signal is high. (Special thanks to vanepp for fixing the PCB holes and other errors)
  KY-004 Key Switch Module: Arduino Key Switch Module Keyes KY-004 is a push button that will output a high signal when pressed.
  MH-Z14: MH-Z14 NDIR Infrared gas module is a common type, small size sensor, using non-dispersive infrared (NDIR) principle to detect the existence of CO2 in the air, with good selectivity, non-oxygen dependant, long life. Built-in temperature sensor can do temperature compensation; and it has digital output and analog voltage output.
