# Fritzing sketch Anaire30ppm_SCD30 (saved by Fritzing 0.9.4)
breadboards: 1

parts:
  Part2 = SCD30
  Mod5 = KY-012 Active Buzzer Module [package="Breakout board"]
  U3 = NodeMCU V1.0
  Grove1 = OLED 128x32

nets:
  VDD: Part2.VDD, Mod5.Vin, U3.3V3, Grove1.VCC
  GND: Part2.GND, Mod5.-, U3.GND, Grove1.GND
  N1: Part2.TX/SCL, U3.D5
  N2: Part2.RX/SDA, U3.D6
  N3: Mod5.S, U3.D0
  N4: U3.D2, Grove1.SCK
  N5: U3.D4, Grove1.SDA

custom parts:
  SCD30: CO2 , humidity, and temperature sensor * Current consumption: 19 mA @ 1 meas. per 2 s. * Digital interface UART or I2C * Company: Sensirion - The Sensor Company Electrical specifications * average current: 19 mA * max. current: 75 mA * DC supply: 3.3 V - 5.5 V Operation conditions * temperature: 0 – 50°C * humidity: 0 – 95 %RH * sensor lifetime: 15 years CO2-sensor: * NDIR CO 2 sensor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
  KY-012 Active Buzzer Module: Active Piezoelectric Buzzer Module KY-012, it produces single-tone sound when signal is high. (Special thanks to vanepp for fixing the PCB holes and other errors)
  NodeMCU V1.0: ESP8266 based NodeMCU
  OLED 128x32: Grove OLED 128X32
