# Fritzing sketch Anaire50ppm_MHZ14A (saved by Fritzing 0.9.4)
breadboards: 1

parts:
  U1 = NodeMCU V1.0
  Mod1 = KY-015 Temperature & Humidity Sensor Module [package="Breakout board"]
  Mod3 = KY-012 Active Buzzer Module [package="Breakout board"]
  MH-Z1 = MH-Z14 [part_number=MH-Z14]
  Grove1 = OLED 128x32  # not connected

nets:
  N1: U1.D0, Mod3.S
  N2: U1.D1, Mod1.S
  VIN: U1.3V3, Mod1.Vin, Mod3.Vin
  N3: U1.GND, Mod1.-, Mod3.-, MH-Z1.15
  N4: U1.D7, MH-Z1.10, MH-Z1.13
  N5: U1.Vin, MH-Z1.14

custom parts:
  NodeMCU V1.0: ESP8266 based NodeMCU
  KY-015 Temperature & Humidity Sensor Module: KY-015 temperature and humidity sensor module, provides a low-latency serial interface to measure humidity and temperature.
  KY-012 Active Buzzer Module: Active Piezoelectric Buzzer Module KY-012, it produces single-tone sound when signal is high. (Special thanks to vanepp for fixing the PCB holes and other errors)
  MH-Z14: MH-Z14 NDIR Infrared gas module is a common type, small size sensor, using non-dispersive infrared (NDIR) principle to detect the existence of CO2 in the air, with good selectivity, non-oxygen dependant, long life. Built-in temperature sensor can do temperature compensation; and it has digital output and analog voltage output.
  OLED 128x32: Grove OLED 128X32
