# Fritzing sketch AnaireSlimSCD30 (saved by Fritzing 0.9.4)
breadboards: 1

parts:
  U1 = NodeMCU V1.0
  Mod1 = KY-015 Temperature & Humidity Sensor Module [package="Breakout board"]
  YwRobot_Power_Supply1 = YwRobot Breadboard Power Supply [part_number=545043]
  Mod3 = KY-012 Active Buzzer Module [package="Breakout board"]
  MH-Z1 = MH-Z14 [part_number=MH-Z14]
  Grove2 = OLED 128x32

nets:
  N1: U1.D0, Mod3.S
  N2: U1.D1, Mod1.S
  N3: U1.GND, YwRobot_Power_Supply1.GND#11, YwRobot_Power_Supply1.GND#12, Mod3.-
  N4: U1.D5, Grove2.SDA
  N5: U1.D6, Grove2.SCK
  N6: U1.D7, MH-Z1.10, MH-Z1.13
  VIN: U1.Vin, YwRobot_Power_Supply1.VCC#5, YwRobot_Power_Supply1.VCC#6, Mod3.Vin
  VIN_2: Mod1.Vin, YwRobot_Power_Supply1.VCC#9, YwRobot_Power_Supply1.VCC#10, MH-Z1.11, MH-Z1.14, Grove2.VCC
  N7: Mod1.-, YwRobot_Power_Supply1.GND#13, YwRobot_Power_Supply1.GND#14, MH-Z1.1, MH-Z1.15, Grove2.GND

custom parts:
  NodeMCU V1.0: ESP8266 based NodeMCU
  KY-015 Temperature & Humidity Sensor Module: KY-015 temperature and humidity sensor module, provides a low-latency serial interface to measure humidity and temperature.
  YwRobot Breadboard Power Supply: The YwRobot Breadboard Power Supply (MB-V2) has two power rails; they can be 5V or 3V3. Power to the module can be provided through the female USB socket or through the A10 (female) 2.1mm power jack.
  KY-012 Active Buzzer Module: Active Piezoelectric Buzzer Module KY-012, it produces single-tone sound when signal is high. (Special thanks to vanepp for fixing the PCB holes and other errors)
  MH-Z14: MH-Z14 NDIR Infrared gas module is a common type, small size sensor, using non-dispersive infrared (NDIR) principle to detect the existence of CO2 in the air, with good selectivity, non-oxygen dependant, long life. Built-in temperature sensor can do temperature compensation; and it has digital output and analog voltage output.
  OLED 128x32: Grove OLED 128X32
