# Fritzing sketch Anaire50ppm_MHZ14A (saved by Fritzing 0.9.4)
breadboards: 1

parts:
  Grove4 = OLED 128x32
  MH-Z4 = MH-Z14 [part_number=MH-Z14]
  U4 = NodeMCU V1.0
  Mod8 = KY-015 Temperature & Humidity Sensor Module [package="Breakout board"]
  Mod9 = KY-012 Active Buzzer Module [package="Breakout board"]

nets:
  GND: Grove4.GND, MH-Z4.15, U4.GND, Mod8.-, Mod9.-
  VIN: Grove4.VCC, U4.3V3, Mod8.Vin, Mod9.Vin
  N1: Grove4.SCK, U4.D5
  N2: Grove4.SDA, U4.D6
  N3: MH-Z4.10, MH-Z4.13, U4.D8
  N4: MH-Z4.14, U4.Vin
  N5: U4.D1, Mod8.S
  N6: U4.D2, Mod9.S

custom parts:
  OLED 128x32: Grove OLED 128X32
  MH-Z14: MH-Z14 NDIR Infrared gas module is a common type, small size sensor, using non-dispersive infrared (NDIR) principle to detect the existence of CO2 in the air, with good selectivity, non-oxygen dependant, long life. Built-in temperature sensor can do temperature compensation; and it has digital output and analog voltage output.
  NodeMCU V1.0: ESP8266 based NodeMCU
  KY-015 Temperature & Humidity Sensor Module: KY-015 temperature and humidity sensor module, provides a low-latency serial interface to measure humidity and temperature.
  KY-012 Active Buzzer Module: Active Piezoelectric Buzzer Module KY-012, it produces single-tone sound when signal is high. (Special thanks to vanepp for fixing the PCB holes and other errors)
